# Fritzing sketch schematic (saved by Fritzing 0.9.5d)
breadboards: 1

parts:
  Part1 = Arduino Nano 33 IOT
  Chirp!_Soil_Moisture_Sensor1 = Chirp! Soil Moisture Sensor v2.7.3
  DS1 = DS18B20 1-Wire Temperature Sensor [part_number=DS18B20]
  R1 = Resistor [tolerance=±5% resistance=4.7k package="1206 [SMD]"]
  Grove1 = Grove OLED 128x96
  R2 = Photocell (LDR) [package=THT]
  R3 = Resistor [tolerance=±1% resistance=10k package="2512 [SMD]"]
  S1 = Pushbutton [package="[THT]"]

nets:
  GND: Part1.GND, Part1.D13~, Chirp!_Soil_Moisture_Sensor1.pin_5, DS1.GND, Grove1.GND, R3.Pin_1, S1.Pin_1, S1.Pin_2
  N1: Part1.D2, DS1.DQ, R1.Pin_1
  N2: Part1.D3~, S1.Pin_3, S1.Pin_4
  N3: Part1.A5, Grove1.SCL
  N4: Part1.A4, Grove1.SDA
  N5: Part1.A1, R2.pin_1, R3.Pin_0
  N6: Part1.A0, Chirp!_Soil_Moisture_Sensor1.pin_3
  3V3: Part1.AREF, Part1.3V3, Chirp!_Soil_Moisture_Sensor1.Pin_1, DS1.VDD, R1.Pin_0, Grove1.VCC, R2.pin_0

custom parts:
  Arduino Nano 33 IOT: The Arduino Nano 33 IoT is the easiest and cheapest point of entry to enhance existing devices (and creating new ones) to be part of the IoT and designing pico-network applications. Whether you are looking at building a sensor network connected to your office or home router, or if you want to create a BLE device sending data to a cellphone, the Nano 33 IoT is your one-stop-solution for many of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
